# Fritzing sketch Rboy (saved by Fritzing 0.9.3b)
circuit board: 6.5cm x 4.5cm
breadboards: 2

parts:
  Part1 = Arduino Nano (Rev3.0)
  GY1 = GY-521 (MPU-6050) [form="♀ (female)" package=THT]
  Squix1 = OLED 0.96" 128x64 I2C SSD1306
  S1 = Pushbutton [package="[THT]"]
  VCC1 = 4 x AAA Battery Mount
  U1 = SWITCH-SPST-2 [package=switch-spst-vertical]

nets:
  GND: Part1.GND, GY1.pin2, GY1.pin7, Squix1.GND, S1.Pin_1, S1.Pin_2, VCC1.-
  N1: Part1.D2, S1.Pin_3, S1.Pin_4
  N2: Part1.VIN, U1.P
  N3: Part1.A5, GY1.pin3, Squix1.SCL
  N4: Part1.A4, GY1.pin4, Squix1.SCA
  3V3: Part1.3V3, GY1.pin1, Squix1.VCC
  N5: VCC1.+, U1.O

custom parts:
  GY-521 (MPU-6050): Placa GY-521 basada en conjunto de acelerómetro+giroscopios MPU-6050
